// Logisim project cpu.circ as structural Verilog: 11 circuits, main circuit main
module main (
);

  wire [15:0] cpu_1_out0, cpu_1_out1, cpu_1_out2, cpu_1_out3, cpu_1_out4, cpu_1_out5, cpu_1_out6, cpu_1_out7;

  CPU cpu_1 (
    .OUT0(cpu_1_out0), .OUT1(cpu_1_out1), .OUT2(cpu_1_out2), .OUT3(cpu_1_out3), .OUT4(cpu_1_out4),
    .OUT5(cpu_1_out5), .OUT6(cpu_1_out6), .OUT7(cpu_1_out7));  // open: IN0, IN1, IN2, IN3, IN4, IN5, IN6, IN7
  DotMatrix #(.matrixcols(8), .matrixrows(16)) dotmatrix_1 (
    .col0(cpu_1_out0), .col1(cpu_1_out1), .col2(cpu_1_out2), .col3(cpu_1_out3), .col4(cpu_1_out4),
    .col5(cpu_1_out5), .col6(cpu_1_out6), .col7(cpu_1_out7));
endmodule

module CPU (
  input  [15:0] IN0,
  input  [15:0] IN1,
  input  [15:0] IN2,
  input  [15:0] IN3,
  input  [15:0] IN4,
  input  [15:0] IN5,
  input  [15:0] IN6,
  input  [15:0] IN7,
  output [15:0] OUT0,
  output [15:0] OUT1,
  output [15:0] OUT2,
  output [15:0] OUT3,
  output [15:0] OUT4,
  output [15:0] OUT5,
  output [15:0] OUT6,
  output [15:0] OUT7
);

  wire and_1_out, and_2_out, and_3_out, button_1_out, CLOCK, clock_1_out, decoder_1_out1, DIS_LIT_SP, HLT,
       IS_LITERAL, N, NEW_INST, nor_1_out, not_1_out, or_1_out, READ_FP, READ_MEM, READ_SP, WRITE_ADDR,
       WRITE_MEM, WRITE_SP, Z;
  wire [1:0] decoder_2_memory, IO_OPS, PC_OPS, REG_OPS;
  wire [2:0] DEST, SRC0, SRC1;
  wire [3:0] ALU, register_1_a_bus, register_1_a_bus_2, register_1_a_bus_3, register_1_a_bus_4, SP_OPS;
  wire [15:0] controlled_buffer_2_out, DATA, DATA_INPUT, INSTRUCTIONS, LITERAL, PC, R0, R1, R2, R3, R4, R5,
       R6, R7, register_1_b_bus, register_2_q, SP;

  Decoder_part #(.select(2)) decoder_1 (.out1(decoder_1_out1), .sel(IO_OPS));  // open: out0, out2, out3, en
  Register register_1 (
    .OP(REG_OPS), .DATA(DATA), .DEST(DEST), .SRC1(SRC1),
    .A_BUS({register_1_a_bus_4, register_1_a_bus_3, register_1_a_bus_2, register_1_a_bus}),
    .B_BUS(register_1_b_bus), .clock(CLOCK), .IO_OP(IO_OPS), .R0(R0), .R1(R1), .R2(R2), .R3(R3), .R4(R4),
    .R5(R5), .R6(R6), .R7(R7), .SRC0(SRC0));
  StackPointer stackpointer_1 (
    .CLOCK(CLOCK), .C(DATA), .OPS(SP_OPS), .SP(SP), .READ(READ_SP), .WRITE(WRITE_SP), .B(DATA_INPUT),
    .READ_FP(READ_FP), .DIS_LIT(DIS_LIT_SP), .PC(PC));
  ProgramCounter programcounter_1 (
    .DATA(DATA), .NEW(NEW_INST), .CLOCK(CLOCK), .PC(PC), .B_BUS(register_1_b_bus), .PC_OP(PC_OPS),
    .READ_FP(READ_FP));
  ALU alu_1 (
    .a({register_1_a_bus_4, register_1_a_bus_3, register_1_a_bus_2, register_1_a_bus}), .b(DATA_INPUT),
    .ops(ALU), .C(DATA), .Z(Z), .N(N));
  assign DATA_INPUT = nor_1_out ? register_1_b_bus : 16'bz;  // Controlled_Buffer controlled_buffer_1
  nor nor_1 (nor_1_out, decoder_1_out1, IS_LITERAL, READ_SP, READ_MEM);
  and and_1 (and_1_out, WRITE_SP, CLOCK);
  assign controlled_buffer_2_out = WRITE_SP ? DATA : 16'bz;  // Controlled_Buffer controlled_buffer_2
  assign DATA_INPUT = READ_SP ? controlled_buffer_2_out : 16'bz;  // Controlled_Buffer controlled_buffer_3
  RAM #(.addrWidth(16), .dataWidth(16)) ram_1 (
    .addr(SP), .data(controlled_buffer_2_out), .sel(1'b1), .clk(and_1_out), .ld(READ_SP));  // open: clr
  not not_1 (not_1_out, DIS_LIT_SP);
  and and_2 (and_2_out, IS_LITERAL, not_1_out);
  assign DATA_INPUT = and_2_out ? LITERAL : 16'bz;  // Controlled_Buffer controlled_buffer_4
  Decoder_InstructionFilter decoder_instructionfilter_1 ();  // open: in_1, instruction, src1, ops, src0, dest, literal
  ROM #(.addrWidth(16), .dataWidth(16)) rom_1 (.addr(PC), .data(INSTRUCTIONS), .sel(1'b1));
  GPIOs gpios_1 (
    .SRC(SRC1), .DEST(DEST), .IN0(IN0), .IN1(IN1), .IN2(IN2), .IN3(IN3), .IN4(IN4), .IN5(IN5), .IN6(IN6),
    .IN7(IN7), .DATA(DATA), .OPS(IO_OPS), .OUT0(OUT0), .OUT1(OUT1), .OUT2(OUT2), .OUT3(OUT3), .OUT4(OUT4),
    .OUT5(OUT5), .OUT6(OUT6), .OUT7(OUT7), .INPUT_DATA(DATA_INPUT), .in_12(CLOCK));
  Decoder decoder_2 (
    .Clock_Input(CLOCK), .Instruction(INSTRUCTIONS), .ALU(ALU), .MEMORY(decoder_2_memory), .SRC0(SRC0),
    .SRC1(SRC1), .LITERAL(LITERAL), .SP(SP_OPS), .PC(PC_OPS), .REG_OPS(REG_OPS), .N(N), .Z(Z),
    .IS_LITERAL(IS_LITERAL), .out_11(NEW_INST), .IO(IO_OPS), .HLT(HLT), .DEST(DEST));
  Register_part #(.width(16), .trigger("falling")) register_2 (
    .D(DATA), .Q(register_2_q), .clk(WRITE_ADDR));  // open: en, clr
  Decoder_part #(.select(2)) decoder_3 (
    .out1(READ_MEM), .out2(WRITE_MEM), .out3(WRITE_ADDR), .sel(decoder_2_memory));  // open: out0, en
  and and_3 (and_3_out, WRITE_MEM, CLOCK);
  Button button_1 (.out(button_1_out));
  Clock clock_1 (.out(clock_1_out));
  RAM #(.addrWidth(16), .dataWidth(16), .bus("separate")) ram_2 (
    .addr(register_2_q), .din(DATA), .data(DATA_INPUT), .sel(1'b1), .clk(and_3_out), .ld(READ_MEM));  // open: str, clr
  or or_1 (or_1_out, button_1_out, clock_1_out);
  and and_4 (CLOCK, or_1_out, ~HLT);  // AND_Gate
  Hex_Digit_Display hex_digit_display_1 (.value({2'b00, REG_OPS}));  // open: dp
  Hex_Digit_Display hex_digit_display_2 (.value({2'b00, IO_OPS}));  // open: dp
  Hex_Digit_Display hex_digit_display_3 (.value({1'b0, DEST}));  // open: dp
  Hex_Digit_Display hex_digit_display_4 (.value(DATA_INPUT[15:12]));  // open: dp
  Hex_Digit_Display hex_digit_display_5 (.value(register_1_a_bus_4));  // open: dp
  Hex_Digit_Display hex_digit_display_6 (.value(DATA[15:12]));  // open: dp
  Hex_Digit_Display hex_digit_display_7 (.value(PC[15:12]));  // open: dp
  Hex_Digit_Display hex_digit_display_8 (.value(DATA_INPUT[11:8]));  // open: dp
  Hex_Digit_Display hex_digit_display_9 (.value(DATA_INPUT[7:4]));  // open: dp
  Hex_Digit_Display hex_digit_display_10 (.value(register_1_a_bus_3));  // open: dp
  Hex_Digit_Display hex_digit_display_11 (.value(register_1_a_bus_2));  // open: dp
  Hex_Digit_Display hex_digit_display_12 (.value(DATA[11:8]));  // open: dp
  Hex_Digit_Display hex_digit_display_13 (.value(DATA[7:4]));  // open: dp
  Hex_Digit_Display hex_digit_display_14 (.value(PC[7:4]));  // open: dp
  Hex_Digit_Display hex_digit_display_15 (.value(PC[11:8]));  // open: dp
  Hex_Digit_Display hex_digit_display_16 (.value({2'b00, PC_OPS}));  // open: dp
  Hex_Digit_Display hex_digit_display_17 (.value({1'b0, SRC0}));  // open: dp
  Hex_Digit_Display hex_digit_display_18 (.value({1'b0, SRC1}));  // open: dp
  Hex_Digit_Display hex_digit_display_19 (.value(DATA_INPUT[3:0]));  // open: dp
  Hex_Digit_Display hex_digit_display_20 (.value(register_1_a_bus));  // open: dp
  Hex_Digit_Display hex_digit_display_21 (.value(DATA[3:0]));  // open: dp
  Hex_Digit_Display hex_digit_display_22 (.value(PC[3:0]));  // open: dp
  Hex_Digit_Display hex_digit_display_23 (.value(ALU));  // open: dp
  Hex_Digit_Display hex_digit_display_24 (.value(R0[15:12]));  // open: dp
  Hex_Digit_Display hex_digit_display_25 (.value(R0[11:8]));  // open: dp
  Hex_Digit_Display hex_digit_display_26 (.value(R1[11:8]));  // open: dp
  Hex_Digit_Display hex_digit_display_27 (.value(R1[15:12]));  // open: dp
  Hex_Digit_Display hex_digit_display_28 (.value(R2[15:12]));  // open: dp
  Hex_Digit_Display hex_digit_display_29 (.value(R2[11:8]));  // open: dp
  Hex_Digit_Display hex_digit_display_30 (.value(R3[11:8]));  // open: dp
  Hex_Digit_Display hex_digit_display_31 (.value(R3[15:12]));  // open: dp
  Hex_Digit_Display hex_digit_display_32 (.value(SP_OPS));  // open: dp
  Hex_Digit_Display hex_digit_display_33 (.value(R0[7:4]));  // open: dp
  Hex_Digit_Display hex_digit_display_34 (.value(R1[7:4]));  // open: dp
  Hex_Digit_Display hex_digit_display_35 (.value(R2[7:4]));  // open: dp
  Hex_Digit_Display hex_digit_display_36 (.value(R3[7:4]));  // open: dp
  Hex_Digit_Display hex_digit_display_37 (.value(R0[3:0]));  // open: dp
  Hex_Digit_Display hex_digit_display_38 (.value(R1[3:0]));  // open: dp
  Hex_Digit_Display hex_digit_display_39 (.value(R2[3:0]));  // open: dp
  Hex_Digit_Display hex_digit_display_40 (.value(R3[3:0]));  // open: dp
  Hex_Digit_Display hex_digit_display_41 (.value(R4[15:12]));  // open: dp
  Hex_Digit_Display hex_digit_display_42 (.value(R5[15:12]));  // open: dp
  Hex_Digit_Display hex_digit_display_43 (.value(R6[15:12]));  // open: dp
  Hex_Digit_Display hex_digit_display_44 (.value(R7[15:12]));  // open: dp
  Hex_Digit_Display hex_digit_display_45 (.value(R4[11:8]));  // open: dp
  Hex_Digit_Display hex_digit_display_46 (.value(R5[11:8]));  // open: dp
  Hex_Digit_Display hex_digit_display_47 (.value(R6[11:8]));  // open: dp
  Hex_Digit_Display hex_digit_display_48 (.value(R7[11:8]));  // open: dp
  Hex_Digit_Display hex_digit_display_49 (.value(R4[3:0]));  // open: dp
  Hex_Digit_Display hex_digit_display_50 (.value(R4[7:4]));  // open: dp
  Hex_Digit_Display hex_digit_display_51 (.value(R5[7:4]));  // open: dp
  Hex_Digit_Display hex_digit_display_52 (.value(R5[3:0]));  // open: dp
  Hex_Digit_Display hex_digit_display_53 (.value(R6[7:4]));  // open: dp
  Hex_Digit_Display hex_digit_display_54 (.value(R6[3:0]));  // open: dp
  Hex_Digit_Display hex_digit_display_55 (.value(R7[3:0]));  // open: dp
  Hex_Digit_Display hex_digit_display_56 (.value(R7[7:4]));  // open: dp

  // Other names for the same wires on the sheet: FP[15:0] = DATA_INPUT; MEM[15:0] = DATA_INPUT;
  //   STACK[15:0] = DATA_INPUT

  // Notes on the sheet:
  //   STACK
  //   INSTRUCTIONS
  //   contents of rom_1 (hex, n*v repeats v):
  //   3 1 7 2 b 4 f 8 13 10 17 20 1b 40 1f 80 a003 14 1803 10 8803 1 8907 1 8a0b 1 8b0f 1 8c13 1 8d17 1
  //   8e1b 1 8f1f 1 2 26 4a 6e 92 b6 da fe a800
  //   RAM
  //   B BUS
  //   A BUS
  //   C BUS
  //   PC
endmodule

module ALU (
  input  [15:0] a,
  input  [15:0] b,
  input  [3:0] ops,
  output [15:0] C,
  output Z,
  output N
);

  wire comparator_1_lt, decoder_1_out0, decoder_1_out1, decoder_1_out2, decoder_1_out3, decoder_1_out4,
       decoder_1_out5, decoder_1_out6, decoder_1_out7, decoder_1_out8, decoder_1_out9, decoder_1_out10,
       decoder_1_out11, decoder_1_out12, nor_1_out, not_1_out, not_3_out;
  wire [15:0] adder_1_out, adder_2_out, and_1_out, divider_1_out, multiplier_1_out, not_2_out, or_1_out,
       shifter_1_out, shifter_2_out, shifter_3_out, subtractor_1_out, subtractor_2_out;

  Decoder_part #(.select(4)) decoder_1 (
    .out0(decoder_1_out0), .out1(decoder_1_out1), .out2(decoder_1_out2), .out3(decoder_1_out3),
    .out4(decoder_1_out4), .out5(decoder_1_out5), .out6(decoder_1_out6), .out7(decoder_1_out7),
    .out8(decoder_1_out8), .out9(decoder_1_out9), .out10(decoder_1_out10), .out11(decoder_1_out11),
    .out12(decoder_1_out12), .sel(ops));  // open: out13, out14, out15, en
  Adder #(.width(16)) adder_1 (.a(b), .b(a), .out(adder_1_out));  // open: cin, cout
  assign C = decoder_1_out1 ? adder_1_out : 16'bz;  // Controlled_Buffer controlled_buffer_1
  Subtractor #(.width(16)) subtractor_1 (.a(b), .b(a), .out(subtractor_1_out));  // open: bin, bout
  assign C = decoder_1_out2 ? subtractor_1_out : 16'bz;  // Controlled_Buffer controlled_buffer_2
  not not_1 (not_1_out, decoder_1_out0);
  nor nor_1 (nor_1_out, C[0], C[1], C[2], C[3], C[4], C[5], C[6], C[7], C[8], C[9], C[10], C[11], C[12], C[13], C[14], C[15]);
  assign C = decoder_1_out0 ? b : 16'bz;  // Controlled_Buffer controlled_buffer_3
  Adder #(.width(16)) adder_2 (.a(16'h1), .b(b), .out(adder_2_out));  // open: cin, cout
  assign C = decoder_1_out3 ? adder_2_out : 16'bz;  // Controlled_Buffer controlled_buffer_4
  D_Flip_Flop #(.trigger("high")) d_ff_1 (.clk(not_1_out), .D(nor_1_out), .Q(Z), .en(1'b1));  // open: Qn, preset, reset
  Subtractor #(.width(16)) subtractor_2 (.a(b), .b(16'h1), .out(subtractor_2_out));  // open: bin, bout
  assign C = decoder_1_out4 ? subtractor_2_out : 16'bz;  // Controlled_Buffer controlled_buffer_5
  assign and_1_out = a & b;  // AND_Gate and_1, 16 bits wide
  assign C = decoder_1_out5 ? and_1_out : 16'bz;  // Controlled_Buffer controlled_buffer_6
  assign or_1_out = a | b;  // OR_Gate or_1, 16 bits wide
  assign C = decoder_1_out6 ? or_1_out : 16'bz;  // Controlled_Buffer controlled_buffer_7
  assign not_2_out = ~b;  // NOT_Gate not_2, 16 bits wide
  assign C = decoder_1_out7 ? not_2_out : 16'bz;  // Controlled_Buffer controlled_buffer_8
  Shifter #(.width(16)) shifter_1 (.in(a), .\dist (b[3:0]), .out(shifter_1_out));
  assign C = decoder_1_out8 ? shifter_1_out : 16'bz;  // Controlled_Buffer controlled_buffer_9
  Comparator #(.width(16)) comparator_1 (.a(b), .b(a), .lt(comparator_1_lt));  // open: gt, eq
  Shifter #(.width(16), .shift("lr")) shifter_2 (.in(a), .\dist (b[3:0]), .out(shifter_2_out));
  not not_3 (not_3_out, decoder_1_out2);
  D_Flip_Flop #(.trigger("high")) d_ff_2 (
    .clk(not_3_out), .D(comparator_1_lt), .Q(N), .en(1'b1));  // open: Qn, preset, reset
  assign C = decoder_1_out9 ? shifter_2_out : 16'bz;  // Controlled_Buffer controlled_buffer_10
  Shifter #(.width(16), .shift("rr")) shifter_3 (.in(a), .\dist (b[3:0]), .out(shifter_3_out));
  assign C = decoder_1_out10 ? shifter_3_out : 16'bz;  // Controlled_Buffer controlled_buffer_11
  Multiplier #(.width(16)) multiplier_1 (.a(a), .b(b), .out(multiplier_1_out));  // open: cin, cout
  assign C = decoder_1_out11 ? multiplier_1_out : 16'bz;  // Controlled_Buffer controlled_buffer_12
  Divider #(.width(16)) divider_1 (.a(a), .b(b), .out(divider_1_out));  // open: upper, rem
  assign C = decoder_1_out12 ? divider_1_out : 16'bz;  // Controlled_Buffer controlled_buffer_13

  // Other names for the same wires on the sheet: A_BUS[15:0] = a; B_BUS[15:0] = b
endmodule

module Decoder (
  input  Clock_Input,
  input  [15:0] Instruction,
  input  N,
  input  Z,
  output [1:0] REG_OPS,
  output [1:0] PC,
  output [3:0] SP,
  output [1:0] MEMORY,
  output [3:0] ALU,
  output HLT,
  output out_11,
  output [15:0] LITERAL,
  output [2:0] SRC0,
  output [2:0] SRC1,
  output [2:0] DEST,
  output [1:0] IO,
  output IS_LITERAL
);

  wire and_1_out, and_2_out, and_4_out, and_5_out, and_6_out, and_7_out, and_8_out, and_9_out, and_10_out,
       Clock, Clock_out, decoder_newchecker_1_out_2, IS_LITERAL_t, IS_STR, NEW, or_3_out, P_DECODE,
       P_EXECUTE, P_EXTEND, READ_MEM, WRITE_ADD, WRITE_MEM;
  wire [1:0] counter_1_q, decoder_instructionfilter_1_ops, multiplexer_3_out;
  wire [2:0] decoder_instructionfilter_1_src1;
  wire [4:0] decoder_instructionfilter_1_instruction;
  wire [7:0] counter_2_q, rom_1_data;
  wire [15:0] register_1_q, rom_2_data;

  Button u_Clock (.out(Clock_out));
  or or_1 (Clock, Clock_Input, Clock_out);
  Register_part #(.width(16)) register_1 (.D(Instruction), .Q(register_1_q), .clk(and_1_out));  // open: en, clr
  and and_1 (and_1_out, Clock, P_DECODE);
  Register_part #(.width(16)) register_2 (.D(Instruction), .Q(LITERAL), .clk(and_2_out));  // open: en, clr
  and and_2 (and_2_out, P_EXTEND, IS_LITERAL_t, Clock);
  Decoder_CheckWriteMemory decoder_checkwritememory_1 (
    .in_1(decoder_instructionfilter_1_instruction), .out_2(IS_STR), .out_3(HLT));
  Decoder_InstructionFilter decoder_instructionfilter_1 (
    .in_1(register_1_q), .instruction(decoder_instructionfilter_1_instruction),
    .src1(decoder_instructionfilter_1_src1), .ops(decoder_instructionfilter_1_ops), .src0(SRC0), .dest(DEST),
    .literal(IS_LITERAL_t));
  and and_3 (IS_LITERAL, IS_LITERAL_t, ~READ_MEM, ~WRITE_MEM);  // AND_Gate
  and and_4 (and_4_out, Clock, ~P_EXECUTE);  // AND_Gate
  and and_5 (and_5_out, NEW, P_EXECUTE);
  Multiplexer #(.width(3)) multiplexer_1 (
    .in0(decoder_instructionfilter_1_src1), .in1(SRC0), .out(SRC1), .sel(and_6_out));  // open: en
  and and_6 (and_6_out, WRITE_MEM, IS_STR);
  Decoder_part #(.select(2)) decoder_1 (
    .out0(P_DECODE), .out1(P_EXTEND), .out2(P_EXECUTE), .sel(counter_1_q));  // open: out3, en
  Counter #(.width(2), .max('h3), .trigger("falling")) counter_1 (
    .Q(counter_1_q), .clk(and_4_out), .clr(and_5_out));  // open: load, D, count, carry
  ROM #(.addrWidth(5)) rom_1 (.addr(decoder_instructionfilter_1_instruction), .data(rom_1_data), .sel(1'b1));
  Multiplexer #(.width(2)) multiplexer_2 (
    .in0(2'b00), .in1(decoder_instructionfilter_1_ops), .out(IO), .sel(P_EXECUTE));  // open: en
  and and_7 (and_7_out, P_EXECUTE, Clock);
  Counter #(.trigger("falling")) counter_2 (
    .load(P_DECODE), .D(rom_1_data), .count(and_7_out), .Q(counter_2_q), .clk(Clock));  // open: carry, clr
  ROM #(.dataWidth(16)) rom_2 (.addr(counter_2_q), .data(rom_2_data), .sel(1'b1));
  Multiplexer #(.width(16)) multiplexer_3 (
    .in0({16{1'b0}}), .in1(rom_2_data), .out({ALU, MEMORY, SP, PC, REG_OPS, multiplexer_3_out}),
    .sel(P_EXECUTE));  // open: en
  Decoder_NewChecker decoder_newchecker_1 (.in_1(rom_2_data), .out_2(decoder_newchecker_1_out_2));
  and and_8 (and_8_out, P_EXTEND, IS_LITERAL_t);
  or or_2 (out_11, and_8_out, P_DECODE);
  Decoder_part #(.select(2)) decoder_2 (
    .out1(READ_MEM), .out2(WRITE_MEM), .out3(WRITE_ADD), .sel(MEMORY));  // open: out0, en
  and and_9 (and_9_out, multiplexer_3_out[1], ~N);  // AND_Gate
  and and_10 (and_10_out, multiplexer_3_out[0], ~Z);  // AND_Gate
  or or_3 (or_3_out, and_9_out, and_10_out);
  or or_4 (NEW, or_3_out, decoder_newchecker_1_out_2);

  // Notes on the sheet:
  //   Addresses
  //   contents of rom_1 (hex, n*v repeats v):
  //   1 3 6 9 b e 11 13 15 17 19 1b 1d 1f 22 25 27 29 2b 2d 2f 36 3b 3d
  //   MicroInstructions
  //   contents of rom_2 (hex, n*v repeats v):
  //   0 c 0 c08 404 0 c08 808 0 20 0 1 20 0 2 20 0 100c 0 200c 0 300c 0 400c 0 500c 0 600c 0 700c 0 88 c0
  //   0 100 44 0 800c 0 900c 0 a00c 0 b00c 0 c00c 0 140 c0 200 1c0 c0 20 0 240 180 100 2a0 0 0 0 2008
endmodule

module Decoder_NewChecker (
  input  [15:0] in_1,
  output out_2
);

  and and_1 (out_2, ~in_1[0], ~in_1[1], ~in_1[2], ~in_1[3], ~in_1[4], ~in_1[5], ~in_1[6], ~in_1[7], ~in_1[8], ~in_1[9], ~in_1[10], ~in_1[11], ~in_1[12], ~in_1[13], ~in_1[14], ~in_1[15]);  // AND_Gate
endmodule

module Decoder_InstructionFilter (
  input  [15:0] in_1,
  output [1:0] ops,
  output literal,
  output [2:0] dest,
  output [2:0] src1,
  output [2:0] src0,
  output [4:0] instruction
);

  and and_1 (literal, in_1[0], in_1[1]);

  assign dest = in_1[4:2];
  assign instruction = in_1[15:11];
  assign ops = in_1[1:0];
  assign src0 = in_1[10:8];
  assign src1 = in_1[7:5];
endmodule

module Decoder_CheckWriteMemory (
  input  [4:0] in_1,
  output out_2,
  output out_3
);

  Decoder_part #(.select(5)) decoder_1 (
    .out2(out_2), .out22(out_3), .sel(in_1));  // open: out0, out1, out3, out4, out5, out6, out7, out8, out9, out10, out11, out12, out13, out14, out15, out16, out17, out18, out19, out20, out21, out23, out24, out25, out26, out27, out28, out29, out30, out31, en
endmodule

module Register (
  input  [1:0] OP,
  input  [1:0] IO_OP,
  input  clock,
  input  [15:0] DATA,
  input  [2:0] DEST,
  input  [2:0] SRC1,
  input  [2:0] SRC0,
  output [15:0] A_BUS,
  output [15:0] B_BUS,
  output [15:0] R0,
  output [15:0] R1,
  output [15:0] R2,
  output [15:0] R3,
  output [15:0] R4,
  output [15:0] R5,
  output [15:0] R6,
  output [15:0] R7
);

  wire and_1_out, and_3_out, and_4_out, and_5_out, and_6_out, and_7_out, and_8_out, and_9_out, and_10_out,
       and_11_out, and_12_out, and_13_out, and_14_out, and_15_out, and_16_out, and_17_out, and_18_out,
       and_19_out, and_20_out, and_21_out, and_22_out, and_23_out, and_24_out, and_25_out, and_26_out,
       decoder_1_out1, decoder_1_out2, decoder_1_out3, decoder_2_out0, decoder_2_out1, decoder_2_out2,
       decoder_2_out3, decoder_2_out4, decoder_2_out5, decoder_2_out6, decoder_2_out7, decoder_3_out0,
       decoder_3_out1, decoder_3_out2, decoder_3_out3, decoder_3_out4, decoder_3_out5, decoder_3_out6,
       decoder_3_out7, decoder_4_out0, decoder_4_out1, decoder_4_out2, decoder_4_out3, decoder_4_out4,
       decoder_4_out5, decoder_4_out6, decoder_4_out7, decoder_5_out2, or_1_out, READ, WRITE;

  Decoder_part #(.select(2)) decoder_1 (
    .out1(decoder_1_out1), .out2(decoder_1_out2), .out3(decoder_1_out3), .sel(OP));  // open: out0, en
  or or_1 (or_1_out, decoder_1_out1, decoder_1_out3);
  or or_2 (READ, decoder_1_out2, decoder_1_out3);
  Decoder_part #(.select(3)) decoder_2 (
    .out0(decoder_2_out0), .out1(decoder_2_out1), .out2(decoder_2_out2), .out3(decoder_2_out3),
    .out4(decoder_2_out4), .out5(decoder_2_out5), .out6(decoder_2_out6), .out7(decoder_2_out7), .sel(DEST));  // open: en
  Decoder_part #(.select(3)) decoder_3 (
    .out0(decoder_3_out0), .out1(decoder_3_out1), .out2(decoder_3_out2), .out3(decoder_3_out3),
    .out4(decoder_3_out4), .out5(decoder_3_out5), .out6(decoder_3_out6), .out7(decoder_3_out7), .sel(SRC1));  // open: en
  Decoder_part #(.select(3)) decoder_4 (
    .out0(decoder_4_out0), .out1(decoder_4_out1), .out2(decoder_4_out2), .out3(decoder_4_out3),
    .out4(decoder_4_out4), .out5(decoder_4_out5), .out6(decoder_4_out6), .out7(decoder_4_out7), .sel(SRC0));  // open: en
  and and_1 (and_1_out, or_1_out, clock);
  Decoder_part #(.select(2)) decoder_5 (.out2(decoder_5_out2), .sel(IO_OP));  // open: out0, out1, out3, en
  and and_2 (WRITE, and_1_out, ~decoder_5_out2);  // AND_Gate
  Register_part #(.width(16), .trigger("falling")) register_1 (.D(DATA), .Q(R0), .clk(and_3_out));  // open: en, clr
  and and_3 (and_3_out, decoder_2_out0, WRITE);
  Register_part #(.width(16), .trigger("falling")) register_2 (.D(DATA), .Q(R1), .clk(and_4_out));  // open: en, clr
  and and_4 (and_4_out, decoder_2_out1, WRITE);
  Register_part #(.width(16), .trigger("falling")) register_3 (.D(DATA), .Q(R2), .clk(and_5_out));  // open: en, clr
  and and_5 (and_5_out, decoder_2_out2, WRITE);
  Register_part #(.width(16), .trigger("falling")) register_4 (.D(DATA), .Q(R3), .clk(and_6_out));  // open: en, clr
  and and_6 (and_6_out, decoder_2_out3, WRITE);
  Register_part #(.width(16), .trigger("falling")) register_5 (.D(DATA), .Q(R4), .clk(and_7_out));  // open: en, clr
  and and_7 (and_7_out, decoder_2_out4, WRITE);
  Register_part #(.width(16), .trigger("falling")) register_6 (.D(DATA), .Q(R5), .clk(and_8_out));  // open: en, clr
  and and_8 (and_8_out, decoder_2_out5, WRITE);
  Register_part #(.width(16), .trigger("falling")) register_7 (.D(DATA), .Q(R6), .clk(and_9_out));  // open: en, clr
  and and_9 (and_9_out, decoder_2_out6, WRITE);
  Register_part #(.width(16), .trigger("falling")) register_8 (.D(DATA), .Q(R7), .clk(and_10_out));  // open: en, clr
  and and_10 (and_10_out, decoder_2_out7, WRITE);
  assign A_BUS = and_11_out ? R0 : 16'bz;  // Controlled_Buffer controlled_buffer_1
  and and_11 (and_11_out, decoder_4_out0, READ);
  assign B_BUS = and_12_out ? R0 : 16'bz;  // Controlled_Buffer controlled_buffer_2
  and and_12 (and_12_out, decoder_3_out0, READ);
  assign A_BUS = and_13_out ? R1 : 16'bz;  // Controlled_Buffer controlled_buffer_3
  and and_13 (and_13_out, decoder_4_out1, READ);
  assign B_BUS = and_14_out ? R1 : 16'bz;  // Controlled_Buffer controlled_buffer_4
  and and_14 (and_14_out, decoder_3_out1, READ);
  assign A_BUS = and_15_out ? R2 : 16'bz;  // Controlled_Buffer controlled_buffer_5
  and and_15 (and_15_out, decoder_4_out2, READ);
  assign B_BUS = and_16_out ? R2 : 16'bz;  // Controlled_Buffer controlled_buffer_6
  and and_16 (and_16_out, decoder_3_out2, READ);
  assign A_BUS = and_17_out ? R3 : 16'bz;  // Controlled_Buffer controlled_buffer_7
  and and_17 (and_17_out, decoder_4_out3, READ);
  assign B_BUS = and_18_out ? R3 : 16'bz;  // Controlled_Buffer controlled_buffer_8
  and and_18 (and_18_out, decoder_3_out3, READ);
  assign A_BUS = and_19_out ? R4 : 16'bz;  // Controlled_Buffer controlled_buffer_9
  and and_19 (and_19_out, decoder_4_out4, READ);
  assign B_BUS = and_20_out ? R4 : 16'bz;  // Controlled_Buffer controlled_buffer_10
  and and_20 (and_20_out, decoder_3_out4, READ);
  assign A_BUS = and_21_out ? R5 : 16'bz;  // Controlled_Buffer controlled_buffer_11
  and and_21 (and_21_out, decoder_4_out5, READ);
  assign B_BUS = and_22_out ? R5 : 16'bz;  // Controlled_Buffer controlled_buffer_12
  and and_22 (and_22_out, decoder_3_out5, READ);
  assign A_BUS = and_23_out ? R6 : 16'bz;  // Controlled_Buffer controlled_buffer_13
  and and_23 (and_23_out, decoder_4_out6, READ);
  assign B_BUS = and_24_out ? R6 : 16'bz;  // Controlled_Buffer controlled_buffer_14
  and and_24 (and_24_out, decoder_3_out6, READ);
  assign A_BUS = and_25_out ? R7 : 16'bz;  // Controlled_Buffer controlled_buffer_15
  and and_25 (and_25_out, decoder_4_out7, READ);
  assign B_BUS = and_26_out ? R7 : 16'bz;  // Controlled_Buffer controlled_buffer_16
  and and_26 (and_26_out, decoder_3_out7, READ);
endmodule

module ProgramCounter (
  input  [15:0] DATA,
  input  NEW,
  input  CLOCK,
  input  [1:0] PC_OP,
  input  READ_FP,
  output [15:0] PC,
  output [15:0] B_BUS
);

  wire decoder_1_out1, decoder_1_out2, decoder_1_out3, READ, WRITE;

  Decoder_part #(.select(2)) decoder_1 (
    .out1(decoder_1_out1), .out2(decoder_1_out2), .out3(decoder_1_out3), .sel(PC_OP));  // open: out0, en
  or or_1 (READ, decoder_1_out1, decoder_1_out3);
  or or_2 (WRITE, decoder_1_out2, decoder_1_out3, READ_FP);
  Counter #(.width(16), .max('hffff), .trigger("falling")) counter_1 (
    .load(WRITE), .D(DATA), .count(NEW), .Q(PC), .clk(CLOCK));  // open: carry, clr
  assign B_BUS = READ ? PC : 16'bz;  // Controlled_Buffer controlled_buffer_1
endmodule

module GPIOs (
  input  [2:0] SRC,
  input  [2:0] DEST,
  input  [15:0] IN0,
  input  [15:0] IN1,
  input  [15:0] IN2,
  input  [15:0] IN3,
  input  [15:0] IN4,
  input  [15:0] IN5,
  input  [15:0] IN6,
  input  [15:0] IN7,
  input  [15:0] DATA,
  input  in_12,
  input  [1:0] OPS,
  output [15:0] OUT0,
  output [15:0] OUT1,
  output [15:0] OUT2,
  output [15:0] OUT3,
  output [15:0] OUT4,
  output [15:0] OUT5,
  output [15:0] OUT6,
  output [15:0] OUT7,
  output [15:0] INPUT_DATA
);

  wire and_1_out, and_2_out, and_3_out, and_4_out, and_5_out, and_6_out, and_7_out, and_8_out, and_9_out,
       and_10_out, and_11_out, and_12_out, and_13_out, and_14_out, and_15_out, and_16_out, and_17_out,
       decoder_1_out0, decoder_1_out1, decoder_1_out2, decoder_1_out3, decoder_1_out4, decoder_1_out5,
       decoder_1_out6, decoder_1_out7, decoder_2_out0, decoder_2_out1, decoder_2_out2, decoder_2_out3,
       decoder_2_out4, decoder_2_out5, decoder_2_out6, decoder_2_out7, READ, WRITE;

  Decoder_part #(.select(3)) decoder_1 (
    .out0(decoder_1_out0), .out1(decoder_1_out1), .out2(decoder_1_out2), .out3(decoder_1_out3),
    .out4(decoder_1_out4), .out5(decoder_1_out5), .out6(decoder_1_out6), .out7(decoder_1_out7), .sel(SRC));  // open: en
  and and_1 (and_1_out, decoder_1_out0, READ);
  and and_2 (and_2_out, decoder_1_out1, READ);
  and and_3 (and_3_out, decoder_1_out2, READ);
  and and_4 (and_4_out, decoder_1_out3, READ);
  and and_5 (and_5_out, decoder_1_out4, READ);
  and and_6 (and_6_out, decoder_1_out5, READ);
  and and_7 (and_7_out, decoder_1_out6, READ);
  and and_8 (and_8_out, decoder_1_out7, READ);
  assign INPUT_DATA = and_1_out ? IN0 : 16'bz;  // Controlled_Buffer controlled_buffer_1
  assign INPUT_DATA = and_2_out ? IN1 : 16'bz;  // Controlled_Buffer controlled_buffer_2
  assign INPUT_DATA = and_3_out ? IN2 : 16'bz;  // Controlled_Buffer controlled_buffer_3
  assign INPUT_DATA = and_4_out ? IN3 : 16'bz;  // Controlled_Buffer controlled_buffer_4
  assign INPUT_DATA = and_5_out ? IN4 : 16'bz;  // Controlled_Buffer controlled_buffer_5
  assign INPUT_DATA = and_6_out ? IN5 : 16'bz;  // Controlled_Buffer controlled_buffer_6
  assign INPUT_DATA = and_7_out ? IN6 : 16'bz;  // Controlled_Buffer controlled_buffer_7
  assign INPUT_DATA = and_8_out ? IN7 : 16'bz;  // Controlled_Buffer controlled_buffer_8
  Decoder_part #(.select(3)) decoder_2 (
    .out0(decoder_2_out0), .out1(decoder_2_out1), .out2(decoder_2_out2), .out3(decoder_2_out3),
    .out4(decoder_2_out4), .out5(decoder_2_out5), .out6(decoder_2_out6), .out7(decoder_2_out7), .sel(DEST));  // open: en
  and and_9 (and_9_out, decoder_2_out0, and_17_out);
  and and_10 (and_10_out, decoder_2_out1, and_17_out);
  and and_11 (and_11_out, decoder_2_out2, and_17_out);
  and and_12 (and_12_out, decoder_2_out3, and_17_out);
  and and_13 (and_13_out, decoder_2_out4, and_17_out);
  and and_14 (and_14_out, decoder_2_out5, and_17_out);
  and and_15 (and_15_out, decoder_2_out6, and_17_out);
  and and_16 (and_16_out, decoder_2_out7, and_17_out);
  Decoder_part #(.select(2)) decoder_3 (.out1(READ), .out2(WRITE), .sel(OPS));  // open: out0, out3, en
  and and_17 (and_17_out, in_12, WRITE);
  Register_part #(.width(16), .trigger("falling")) register_1 (.D(DATA), .Q(OUT0), .clk(and_9_out));  // open: en, clr
  Register_part #(.width(16), .trigger("falling")) register_2 (.D(DATA), .Q(OUT1), .clk(and_10_out));  // open: en, clr
  Register_part #(.width(16), .trigger("falling")) register_3 (.D(DATA), .Q(OUT2), .clk(and_11_out));  // open: en, clr
  Register_part #(.width(16), .trigger("falling")) register_4 (.D(DATA), .Q(OUT3), .clk(and_12_out));  // open: en, clr
  Register_part #(.width(16), .trigger("falling")) register_5 (.D(DATA), .Q(OUT4), .clk(and_13_out));  // open: en, clr
  Register_part #(.width(16), .trigger("falling")) register_6 (.D(DATA), .Q(OUT5), .clk(and_14_out));  // open: en, clr
  Register_part #(.width(16), .trigger("falling")) register_7 (.D(DATA), .Q(OUT6), .clk(and_15_out));  // open: en, clr
  Register_part #(.width(16), .trigger("falling")) register_8 (.D(DATA), .Q(OUT7), .clk(and_16_out));  // open: en, clr

  // Other names for the same wires on the sheet: CLOCK = in_12
endmodule

module StackPointer (
  input  [15:0] PC,
  input  CLOCK,
  input  [15:0] C,
  input  [3:0] OPS,
  output [15:0] B,
  output [15:0] SP,
  output READ,
  output WRITE,
  output READ_FP,
  output DIS_LIT
);

  wire and_1_out, dec, fp_read_sp, fp_read_stack, fp_write_sp, fp_write_stack, inc, load_return, or_1_out,
       or_2_out, or_3_out, or_7_out, read_t, write_t;
  wire [15:0] controlled_buffer_1_out, multiplexer_1_out, register_1_q;

  Decoder_part #(.select(4)) decoder_1 (
    .out1(read_t), .out2(write_t), .out3(inc), .out4(dec), .out5(load_return), .out6(fp_read_stack),
    .out7(fp_read_sp), .out8(fp_write_stack), .out9(fp_write_sp), .out10(READ_FP), .sel(OPS));  // open: out0, out11, out12, out13, out14, out15, en
  assign controlled_buffer_1_out = fp_read_sp ? SP : 16'bz;  // Controlled_Buffer controlled_buffer_1
  assign controlled_buffer_1_out = fp_read_stack ? C : 16'bz;  // Controlled_Buffer controlled_buffer_2
  or or_1 (or_1_out, fp_write_sp, dec);
  or or_2 (or_2_out, dec, inc);
  Register_part #(.width(16), .trigger("falling")) register_1 (
    .D(controlled_buffer_1_out), .Q(register_1_q), .clk(and_1_out));  // open: en, clr
  and and_1 (and_1_out, CLOCK, or_3_out);
  Counter #(.width(16), .max('hffff), .trigger("falling")) counter_1 (
    .load(or_1_out), .D(C), .count(or_2_out), .Q(SP), .clk(CLOCK));  // open: carry, clr
  or or_3 (or_3_out, fp_read_stack, fp_read_sp);
  or or_4 (READ, READ_FP, fp_read_stack, read_t);
  or or_5 (WRITE, fp_write_stack, write_t, load_return);
  or or_6 (DIS_LIT, fp_write_stack, load_return);
  assign B = or_7_out ? multiplexer_1_out : 16'bz;  // Controlled_Buffer controlled_buffer_3
  Multiplexer #(.width(16)) multiplexer_1 (
    .in0(register_1_q), .in1(PC), .out(multiplexer_1_out), .sel(load_return));  // open: en
  or or_7 (or_7_out, fp_write_stack, load_return, fp_write_sp);

  // Other names for the same wires on the sheet: write_to_pc = READ_FP

  // Notes on the sheet:
  //   FRAME POINTER
  //   STACK POINTER
endmodule
